// Digital circuit Ü01-Halb-Addierer.dig as structural Verilog
module \Ü01_Halb_Addierer  (
  input  A,
  input  B,
  output S,
  output \Ü 
);

  wire and_1_out, and_2_out;

  and and_1 (and_1_out, A, ~B);  // And
  and and_2 (and_2_out, ~A, B);  // And
  and and_3 (\Ü , A, B);
  or or_1 (S, and_1_out, and_2_out);
endmodule

/* Test case:
A B S Ü 

 0 0 0 0
 0 1 1 0
 1 0 1 0
 1 1 0 1
*/
