// Digital circuit Ü01-Voll-Addierer.dig as structural Verilog
module \Ü01_Voll_Addierer  (
  input  A,
  input  B,
  input  C,
  output S,
  output \Ü 
);

  wire and_1_out, and_2_out, and_3_out, and_4_out, and_5_out, and_6_out, and_7_out, and_8_out, and_9_out,
       and_10_out, and_11_out, and_12_out, and_13_out, and_14_out, and_15_out, and_16_out, or_1_out,
       or_2_out, or_3_out, or_4_out;

  and and_1 (and_1_out, A, ~B);  // And
  and and_2 (and_2_out, ~A, B);  // And
  and and_3 (and_3_out, ~A, ~B);  // And
  and and_4 (and_4_out, A, B);
  and and_5 (and_5_out, A, B);
  and and_6 (and_6_out, ~A, B);  // And
  and and_7 (and_7_out, A, ~B);  // And
  and and_8 (and_8_out, A, B);
  and and_9 (and_9_out, and_1_out, ~C);  // And
  and and_10 (and_10_out, and_2_out, ~C);  // And
  and and_11 (and_11_out, and_3_out, C);
  and and_12 (and_12_out, and_4_out, C);
  and and_13 (and_13_out, and_5_out, ~C);  // And
  and and_14 (and_14_out, and_6_out, C);
  and and_15 (and_15_out, and_7_out, C);
  and and_16 (and_16_out, and_8_out, C);
  or or_1 (or_1_out, and_9_out, and_10_out);
  or or_2 (or_2_out, and_11_out, and_12_out);
  or or_3 (or_3_out, and_13_out, and_14_out);
  or or_4 (or_4_out, and_15_out, and_16_out);
  or or_5 (S, or_1_out, or_2_out);
  or or_6 (\Ü , or_3_out, or_4_out);
endmodule

/* Test case:
A B C S Ü 

 0 0 0 0 0
 0 0 1 1 0
 0 1 0 1 0
 0 1 1 0 1
 1 0 0 1 0
 1 0 1 0 1
 1 1 0 0 1
 1 1 1 1 1
*/
