// Digital circuit Ü02-Komparator.dig as structural Verilog
module \Ü02_Komparator  (
  input  A,
  input  B,
  output Y1,
  output Y2,
  output Y3
);

  wire and_2_out, and_3_out, not_1_out, not_2_out;

  not not_1 (not_1_out, A);
  not not_2 (not_2_out, B);
  and and_1 (Y1, not_1_out, B);
  and and_2 (and_2_out, A, B);
  and and_3 (and_3_out, not_1_out, not_2_out);
  and and_4 (Y3, A, not_2_out);
  or or_1 (Y2, and_2_out, and_3_out);

  // Notes on the sheet:
  //   Y1: A<B
  //   Y2: A=B
  //   Y3: A>B
endmodule

/* Test case:
A B Y1 Y2 Y3 

 0 0 0 1 0
 0 1 1 0 0
 1 0 0 0 1
 1 1 0 1 0
*/
