// Digital circuit Ü01-Inkrementierer.dig as structural Verilog
module \Ü01_Inkrementierer  (
  input  A0,
  input  A1,
  input  B0,
  input  B1,
  output S0,
  output S1,
  output \Ü 
);

  wire \ü01_halb_addierer_1_ü ;

  Seven_Seg_Hex seven_seg_hex_1 (.d({2'b00, A1, A0}), .dp(1'b1));
  Seven_Seg_Hex seven_seg_hex_2 (.d({2'b00, B1, B0}), .dp(1'b1));
  \Ü01_Halb_Addierer  \u_ü01_halb_addierer_1  (.A(A0), .B(B0), .S(S0), .\Ü (\ü01_halb_addierer_1_ü ));
  \Ü01_Voll_Addierer  \u_ü01_voll_addierer_1  (.A(\ü01_halb_addierer_1_ü ), .B(A1), .C(B1), .S(S1), .\Ü (\Ü ));
  Seven_Seg_Hex seven_seg_hex_3 (.d({1'b0, \Ü , S1, S0}), .dp(1'b1));
endmodule

/* Test case:
A0 A1 B0 B1 S0 S1 Ü 

 0 0 0 0 0 0 0
 0 0 0 1 0 1 0
 0 0 1 0 1 0 0
 0 0 1 1 1 1 0
 0 1 0 0 0 1 0
 0 1 0 1 0 0 1
 0 1 1 0 1 1 0
 0 1 1 1 1 0 1
 1 0 0 0 1 0 0
 1 0 0 1 1 1 0
 1 0 1 0 0 1 0
 1 0 1 1 0 0 1
 1 1 0 0 1 1 0
 1 1 0 1 1 0 1
 1 1 1 0 0 0 1
 1 1 1 1 0 1 1
*/
